# Fritzing sketch scheme (saved by Fritzing 0.9.5d)

parts:
  LED1 = RGB LED - (4 legs) [package="5 mm [THT]"]
  Компонент1 = Arduino Nano (Rev3.0)
  R1 = Resistor [tolerance=±5% resistance=470 package=THT]
  S2 = Pushbutton [package="[THT]"]  # not connected
  LED2 = RGB LED - (4 legs) [package="5 mm [THT]"]
  LED3 = RGB LED - (4 legs) [package="5 mm [THT]"]
  R2 = Resistor [tolerance=±5% resistance=10k package=THT]

nets:
  N1: LED1.red_cathode, R1.Pin_1
  N2: LED1.blue_cathode, LED2.red_cathode
  N3: Компонент1.D9, R2.Pin_0
  N4: Компонент1.D13/SCK, R1.Pin_0
  N5: LED2.blue_cathode, LED3.red_cathode

notes:
  DIN
  DOUT
  470
  10k
  +5v
  GND
  1
  2
  n
